// Logisim project CPU.circ as structural Verilog: 13 circuits, main circuit main
module main (
  input  Reset,
  input  [7:0] RAM_Addr_Monitor,
  input  Monitor_Mode
);

  wire clock_1_out, comparator_1_eq, control_unit_1_alu_store, control_unit_1_hlt, control_unit_1_inc,
       control_unit_1_inc_b, control_unit_1_ir_load, control_unit_1_jz_out, control_unit_1_pc_inc,
       control_unit_1_pc_load, control_unit_1_ram_re, control_unit_1_ram_we, control_unit_1_rega_load,
       control_unit_1_regb_load, control_unit_1_vram_we, control_unit_1_vram_we_b, not_1_out, or_1_out,
       or_2_out, register_1_q, register_2_q, rgb_video_1_p1, rgb_video_1_p2, undriven_2;
  wire [2:0] control_unit_1_alu_op;
  wire [3:0] ram8_1_out_5, ram8_1_out_5_2, rgb_video_1_p3, rgb_video_1_p4, undriven_5, undriven_6;
  wire [7:0] adder_2_out, instructionregister_1_opcode, multiplexer_1_out, multiplexer_2_out,
       multiplexer_3_out, multiplexer_4_out, multiplexer_6_out, multiplexer_7_out, multiplexer_8_out,
       programcounter_1_pc, Reg_A_q, RegB_q, rgbled_1_p1, undriven, undriven_3, undriven_4;
  wire [15:0] rom_1_data;

  // RGBLED rgbled_1: pin names not known; wires that end beside it: rgbled_1_p1
  DotMatrix dotmatrix_1 ();  // open: col0, col1, col2, col3, col4
  Adder adder_1 (.a(Reg_A_q), .b(8'h1), .out(rgbled_1_p1));  // open: cin, cout
  ProgramCounter programcounter_1 (
    .CLK(rgb_video_1_p1), .Reset(Reset), .Inc(control_unit_1_pc_inc), .D(undriven), .Load(or_1_out),
    .PC(programcounter_1_pc));
  Rigester8 RegB (
    .D(multiplexer_7_out), .CLK(rgb_video_1_p1), .Reset(Reset), .Load(control_unit_1_regb_load), .Q(RegB_q));
  ALU alu_1 (.A(Reg_A_q), .B(RegB_q), .Op(control_unit_1_alu_op));  // open: out_4, Result
  InstructionRegister instructionregister_1 (
    .Instruction(rom_1_data), .Load(control_unit_1_ir_load), .CLK(rgb_video_1_p1), .Reset(Reset),
    .Operand(RegB_q), .Opcode(instructionregister_1_opcode));
  ROM #(.dataWidth(16)) rom_1 (.addr(programcounter_1_pc), .data(rom_1_data));
  Multiplexer #(.width(8)) multiplexer_1 (
    .in0(undriven_3), .out(multiplexer_1_out), .sel(control_unit_1_alu_store));  // open: in1
  Rigester8 Reg_A (.D(multiplexer_6_out), .CLK(rgb_video_1_p1), .Reset(Reset), .Load(or_2_out), .Q(Reg_A_q));
  // Probe on undriven_3
  Multiplexer #(.width(8)) multiplexer_2 (
    .in0(undriven_4), .in1(multiplexer_1_out), .out(multiplexer_2_out), .sel(control_unit_1_inc));
  // RGB_Video #(.height(16), .scale(8), .width(16)) rgb_video_1: pin names not known; wires that end beside it: rgb_video_1_p1, rgb_video_1_p2, rgb_video_1_p3, rgb_video_1_p4, Reg_A_q
  // Probe on multiplexer_6_out
  // Probe on multiplexer_3_out
  // Probe on {ram8_1_out_5_2, ram8_1_out_5}
  and and_1 (rgb_video_1_p1, not_1_out, clock_1_out);
  Multiplexer #(.width(8)) multiplexer_3 (
    .in0(multiplexer_2_out), .in1(undriven_3), .out(multiplexer_3_out), .sel(control_unit_1_rega_load));
  Clock clock_1 (.out(clock_1_out));
  // Probe on control_unit_1_rega_load
  Multiplexer #(.width(8)) multiplexer_4 (
    .in0(multiplexer_3_out), .in1({ram8_1_out_5_2, ram8_1_out_5}), .out(multiplexer_4_out), .sel(register_1_q));
  // Probe on register_1_q
  not not_1 (not_1_out, control_unit_1_hlt);
  Adder adder_2 (.a(RegB_q), .b(8'h1), .out(adder_2_out));  // open: cin, cout
  Multiplexer #(.width(8)) multiplexer_5 (
    .in0(undriven), .in1(RegB_q), .out({rgb_video_1_p4, rgb_video_1_p3}), .sel(control_unit_1_vram_we_b));
  Multiplexer #(.width(8)) multiplexer_6 (
    .in0(multiplexer_4_out), .in1({ram8_1_out_5_2, ram8_1_out_5}), .out(multiplexer_6_out), .sel(register_1_q));
  Multiplexer #(.width(8)) multiplexer_7 (
    .in0(undriven_3), .in1(adder_2_out), .out(multiplexer_7_out), .sel(control_unit_1_inc_b));
  Multiplexer #(.width(8)) multiplexer_8 (
    .in0(undriven_3), .in1(RAM_Addr_Monitor), .out(multiplexer_8_out), .sel(Monitor_Mode));
  Register #(.width(1)) register_1 (
    .D(control_unit_1_ram_re), .en(1'b1), .clk(undriven_2), .Q(register_1_q), .clr(Reset));
  Comparator #(.mode("unsigned")) comparator_1 (.a(Reg_A_q), .b({8{1'b0}}), .eq(comparator_1_eq));  // open: gt, lt
  Hex_Digit_Display hex_digit_display_1 (.value(ram8_1_out_5_2));  // open: dp
  Hex_Digit_Display hex_digit_display_2 (.value(ram8_1_out_5));  // open: dp
  RAM8 ram8_1 (
    .Address(multiplexer_8_out), .WE(control_unit_1_ram_we), .CLK(rgb_video_1_p1), .DataIn(Reg_A_q),
    .out_5({ram8_1_out_5_2, ram8_1_out_5}));
  or or_1 (or_1_out, control_unit_1_pc_load, control_unit_1_jz_out);
  Register #(.width(1)) register_2 (
    .D(control_unit_1_ram_re), .en(1'b1), .clk(undriven_2), .Q(register_2_q), .clr(Reset));
  or or_2 (or_2_out, register_2_q, control_unit_1_rega_load);
  // Probe on {undriven_6, undriven_5}
  // Probe on Reg_A_q
  Control_Unit control_unit_1 (
    .Opcode(instructionregister_1_opcode), .ZeroFlag(comparator_1_eq), .IR_Load(control_unit_1_ir_load),
    .RegB_Load(control_unit_1_regb_load), .ALU_Store(control_unit_1_alu_store),
    .ALU_Op(control_unit_1_alu_op), .HLT(control_unit_1_hlt), .PC_Inc(control_unit_1_pc_inc),
    .RAM_WE(control_unit_1_ram_we), .RegA_Load(control_unit_1_rega_load), .PC_Load(control_unit_1_pc_load),
    .JZ_OUT(control_unit_1_jz_out), .VRAM_WE(control_unit_1_vram_we), .Inc(control_unit_1_inc),
    .VRAM_WE_B(control_unit_1_vram_we_b), .INC_B(control_unit_1_inc_b), .RAM_RE(control_unit_1_ram_re));
  or or_3 (rgb_video_1_p2, control_unit_1_vram_we, control_unit_1_vram_we_b);

  // Notes on the sheet:
  //   contents of rom_1 (hex, n*v repeats v):
  //   10d5 0 6007 0 6008 0 6017 0 6018 0 6027 0 6028 0 6037 0 6038 0 6040 0 6041 0 6042 0 6043 0 6044 0
  //   6045 0 6046 0 6047 0 6048 0 6049 0 604a 0 604b 0 604c 0 604d 0 604e 0 604f 0 6055 0 6056 0 6057 0
  //   6058 0 6059 0 605a 0 605b 0 605c 0 605d 0 605e 0 6065 0 6066 0 6067 0 6068 0 6069 0 606a 0 606b 0
  //   606c 0 606d 0 6074 0 6075 0 6076 0 607b 0 607c 0 607d 0 6083 0 6084 0 608b 0 608c 0 6092 0 6093 0
  //   609b 0 609c 0 60a1 0 60a2 0 60ab 0 60ac 0 60b1 0 60b2 0 60bb 0 60bc 0 60c2 0 60c3 0 60ca 0 60cb 0
  //   60d4 0 60d5 0 60d6 0 60d7 0 60d8 0 60d9 0 60da 0 60db 0 f000
endmodule

module Full_Adder (
  input  A,
  input  B,
  input  Cin,
  output Sum,
  output Cout
);

  wire and_1_out, and_2_out, xor_1_out;

  xor xor_1 (xor_1_out, A, B);
  and and_1 (and_1_out, Cin, xor_1_out);
  and and_2 (and_2_out, A, B);
  xor xor_2 (Sum, xor_1_out, Cin);
  or or_1 (Cout, and_1_out, and_2_out);
endmodule

module Adder8bit (
  input  B2,
  input  B1,
  input  A0,
  input  B0,
  input  A6,
  input  A2,
  input  A1,
  input  B3,
  input  A7,
  input  B4,
  input  B7,
  input  B5,
  input  B6,
  input  A3,
  input  A5,
  input  A4,
  input  Cin,
  output Cout,
  output S5,
  output S6,
  output S7,
  output S0,
  output S1,
  output S2,
  output S3,
  output S4
);

  wire full_adder_1_cout, full_adder_2_cout, full_adder_3_cout, full_adder_4_cout, full_adder_5_cout,
       full_adder_6_cout, full_adder_7_cout;

  Full_Adder full_adder_1 (.A(A0), .B(B0), .Cin(Cin), .Sum(S0), .Cout(full_adder_1_cout));
  Full_Adder full_adder_2 (.A(A1), .B(B1), .Cin(full_adder_1_cout), .Sum(S1), .Cout(full_adder_2_cout));
  Full_Adder full_adder_3 (.A(A2), .B(B2), .Cin(full_adder_2_cout), .Sum(S2), .Cout(full_adder_3_cout));
  Full_Adder full_adder_4 (.A(A3), .B(B3), .Cin(full_adder_3_cout), .Sum(S3), .Cout(full_adder_4_cout));
  Full_Adder full_adder_5 (.A(A4), .B(B4), .Cin(full_adder_4_cout), .Sum(S4), .Cout(full_adder_5_cout));
  Full_Adder full_adder_6 (.A(A5), .B(B5), .Cin(full_adder_5_cout), .Sum(S5), .Cout(full_adder_6_cout));
  Full_Adder full_adder_7 (.A(A6), .B(B6), .Cin(full_adder_6_cout), .Sum(S6), .Cout(full_adder_7_cout));
  Full_Adder full_adder_8 (.A(A7), .B(B7), .Cin(full_adder_7_cout), .Sum(S7), .Cout(Cout));
endmodule

module ALU (
  input  [7:0] A,
  input  [7:0] B,
  input  [2:0] Op,
  output out_4,
  output [7:0] Result
);

  wire [7:0] adder_1_out, and_1_out, not_1_out, or_1_out, shifter_1_out, shifter_2_out, subtractor_1_out,
       xor_1_out;

  Adder adder_1 (.a(A), .b(B), .out(adder_1_out), .cout(out_4));  // open: cin
  Subtractor subtractor_1 (.a(A), .b(B), .out(subtractor_1_out));  // open: bin, bout
  assign and_1_out = A & B;  // AND_Gate and_1, 8 bits wide
  assign xor_1_out = A ^ B;  // XOR_Gate xor_1, 8 bits wide
  assign or_1_out = A | B;  // OR_Gate or_1, 8 bits wide
  Shifter shifter_1 (.in(A), .\dist (3'b001), .out(shifter_1_out));
  Shifter #(.shift("lr")) shifter_2 (.in(A), .\dist (3'b001), .out(shifter_2_out));
  assign not_1_out = ~A;  // NOT_Gate not_1, 8 bits wide
  Multiplexer #(.select(3), .width(8)) multiplexer_1 (
    .in0(adder_1_out), .in1(subtractor_1_out), .in2(and_1_out), .in3(or_1_out), .in4(xor_1_out),
    .in5(not_1_out), .in6(shifter_1_out), .in7(shifter_2_out), .out(Result), .sel(Op));
  Hex_Digit_Display hex_digit_display_1 (.value(Result[7:4]));  // open: dp
  Hex_Digit_Display hex_digit_display_2 (.value(Result[3:0]));  // open: dp
endmodule

module Rigester8 (
  input  [7:0] D,
  input  CLK,
  input  Reset,
  input  Load,
  output [7:0] Q
);

  Register register_1 (.D(D), .en(Load), .clk(CLK), .Q(Q), .clr(Reset));
  Hex_Digit_Display hex_digit_display_1 (.value(Q[3:0]));  // open: dp
  Hex_Digit_Display hex_digit_display_2 (.value(Q[7:4]));  // open: dp
endmodule

module ProgramCounter (
  input  CLK,
  input  Reset,
  input  Inc,
  input  [7:0] D,
  input  Load,
  output [7:0] PC
);

  wire [7:0] adder_1_out, multiplexer_1_out, multiplexer_2_out;

  Register register_1 (.D(multiplexer_2_out), .en(1'b1), .clk(CLK), .Q(PC), .clr(Reset));
  Hex_Digit_Display hex_digit_display_1 (.value(PC[7:4]));  // open: dp
  Hex_Digit_Display hex_digit_display_2 (.value(PC[3:0]));  // open: dp
  Adder adder_1 (.a(PC), .b(8'h1), .out(adder_1_out));  // open: cin, cout
  Multiplexer #(.width(8)) multiplexer_1 (.in0(PC), .in1(adder_1_out), .out(multiplexer_1_out), .sel(Inc));
  Multiplexer #(.width(8)) multiplexer_2 (.in0(multiplexer_1_out), .in1(D), .out(multiplexer_2_out), .sel(Load));
endmodule

module Half_Adder (
  input  A,
  input  B,
  output out_3,
  output out_4
);

  xor xor_1 (out_3, A, B);
  and and_1 (out_4, A, B);
endmodule

module ROM8 (
  input  [7:0] Address,
  output [15:0] Instruction
);

  ROM #(.dataWidth(16)) rom_1 (.addr(Address), .data(Instruction));
  Hex_Digit_Display hex_digit_display_1 (.value(Instruction[15:12]));  // open: dp
  Hex_Digit_Display hex_digit_display_2 (.value(Instruction[7:4]));  // open: dp
  Hex_Digit_Display hex_digit_display_3 (.value(Instruction[11:8]));  // open: dp
  Hex_Digit_Display hex_digit_display_4 (.value(Instruction[3:0]));  // open: dp

  // Notes on the sheet:
  //   contents of rom_1 (hex, n*v repeats v):
  //   10e2 0 6004 0 6005 0 6006 0 6007 0 6008 0 6009 0 600a 0 600b 0 6013 0 601c 0 6022 0 602d 0 6032 0
  //   603d 0 6042 0 604d 0 6052 0 605d 0 6062 0 606d 0 6072 0 607d 0 6074 0 6075 0 6076 0 6077 0 6078 0
  //   6079 0 607a 0 607b 0 607c 0 6083 0 608c 0 6092 0 609d 0 60a2 0 60ad 0 60b2 0 60bd 0 60c2 0 60cd 0
  //   60d3 0 60dc 0 60e3 0 60ec 0 60f4 0 60f5 0 60f6 0 60f7 0 60f8 0 60f9 0 60fa 0 60fb 0 6003 0 600c 0
  //   6014 0 601b 0 6063 0 606c 0 60d2 0 60dd 0 60e2 0 60ed 0 f000
endmodule

module InstructionRegister (
  input  [15:0] Instruction,
  input  Load,
  input  CLK,
  input  Reset,
  output [7:0] Operand,
  output [7:0] Opcode
);

  Hex_Digit_Display hex_digit_display_1 (.value(Opcode[7:4]));  // open: dp
  Register #(.width(16)) register_1 (.D(Instruction), .en(Load), .clk(CLK), .Q({Opcode, Operand}), .clr(Reset));
  Hex_Digit_Display hex_digit_display_2 (.value(Opcode[3:0]));  // open: dp
  Hex_Digit_Display hex_digit_display_3 (.value(Operand[7:4]));  // open: dp
  Hex_Digit_Display hex_digit_display_4 (.value(Operand[3:0]));  // open: dp
endmodule

module Control_Unit (
  input  [7:0] Opcode,
  input  ZeroFlag,
  output IR_Load,
  output RegB_Load,
  output ALU_Store,
  output [2:0] ALU_Op,
  output HLT,
  output PC_Inc,
  output RAM_WE,
  output RegA_Load,
  output PC_Load,
  output JZ_OUT,
  output VRAM_WE,
  output Inc,
  output VRAM_WE_B,
  output INC_B,
  output RAM_RE
);

  wire comparator_1_eq, comparator_2_eq, comparator_3_eq, comparator_4_eq, comparator_5_eq, comparator_6_eq,
       comparator_10_eq, not_1_out;

  Comparator #(.mode("unsigned")) comparator_1 (.a(Opcode), .b(8'h10), .eq(comparator_1_eq));  // open: gt, lt
  Comparator #(.mode("unsigned")) comparator_2 (.a(Opcode), .b(8'h11), .eq(comparator_2_eq));  // open: gt, lt
  Comparator #(.mode("unsigned")) comparator_3 (.a(Opcode), .b(8'h20), .eq(comparator_3_eq));  // open: gt, lt
  Comparator #(.mode("unsigned")) comparator_4 (.a(Opcode), .b(8'h21), .eq(comparator_4_eq));  // open: gt, lt
  Comparator #(.mode("unsigned")) comparator_5 (.a(Opcode), .b(8'h22), .eq(comparator_5_eq));  // open: gt, lt
  Comparator #(.mode("unsigned")) comparator_6 (.a(Opcode), .b(8'h23), .eq(comparator_6_eq));  // open: gt, lt
  Comparator #(.mode("unsigned")) comparator_7 (.a(Opcode), .b(8'hf0), .eq(HLT));  // open: gt, lt
  Comparator #(.mode("unsigned")) comparator_8 (.a(Opcode), .b(8'h30), .eq(RAM_WE));  // open: gt, lt
  Comparator #(.mode("unsigned")) comparator_9 (.a(Opcode), .b(8'h40), .eq(PC_Load));  // open: gt, lt
  Comparator #(.mode("unsigned")) comparator_10 (.a(Opcode), .b(8'h50), .eq(comparator_10_eq));  // open: gt, lt
  Comparator #(.mode("unsigned")) comparator_11 (.a(Opcode), .b(8'h60), .eq(VRAM_WE));  // open: gt, lt
  Comparator #(.mode("unsigned")) comparator_12 (.a(Opcode), .b(8'h70), .eq(Inc));  // open: gt, lt
  Comparator #(.mode("unsigned")) comparator_13 (.a(Opcode), .b(8'h61), .eq(VRAM_WE_B));  // open: gt, lt
  Comparator #(.mode("unsigned")) comparator_14 (.a(Opcode), .b(8'h71), .eq(INC_B));  // open: gt, lt
  Comparator #(.mode("unsigned")) comparator_15 (.a(Opcode), .b(8'h80), .eq(RAM_RE));  // open: gt, lt
  and and_1 (JZ_OUT, comparator_10_eq, ZeroFlag);
  not not_1 (not_1_out, HLT);
  or or_1 (ALU_Op[0], comparator_4_eq, comparator_6_eq);
  or or_2 (ALU_Op[1], comparator_5_eq, comparator_6_eq);
  and and_2 (PC_Inc, 1'b1, not_1_out);
  or or_3 (ALU_Store, comparator_3_eq, comparator_4_eq, Inc, comparator_5_eq, comparator_6_eq);
  or or_4 (RegB_Load, comparator_2_eq, INC_B);
  or or_5 (RegA_Load, comparator_1_eq, comparator_3_eq, comparator_4_eq, comparator_5_eq, comparator_6_eq, Inc, RAM_RE);

  assign ALU_Op[2] = 1'b0;
  assign IR_Load = 1'b1;
endmodule

module RAM8 (
  input  [7:0] Address,
  input  WE,
  input  CLK,
  input  [7:0] DataIn,
  output [7:0] out_5
);

  RAM ram_1 (.addr(Address), .we(WE), .oe(1'b1), .clk(CLK), .din(DataIn), .dout(out_5));
endmodule

module VideoRAM (
  input  WE,
  input  Reset,
  input  [7:0] DataIn,
  input  CLK,
  input  [7:0] Address
);

  wire or_1_out;

  or or_1 (or_1_out, Reset, 1'b0);
  // RGB_Video #(.height(16), .reset("Synchronous"), .scale(8), .width(16)) rgb_video_1: pin names not known; wires that end beside it: or_1_out, CLK, WE, Address[7:4], Address[3:0], DataIn
endmodule

module main2 (
  input  Reset,
  input  [7:0] RAM_Addr_Monitor,
  input  Monitor_Mode
);

  wire and_1_out, clock_1_out, comparator_1_eq, control_unit_1_alu_store, control_unit_1_hlt,
       control_unit_1_inc, control_unit_1_inc_b, control_unit_1_ir_load, control_unit_1_jz_out,
       control_unit_1_pc_inc, control_unit_1_pc_load, control_unit_1_ram_we, control_unit_1_rega_load,
       control_unit_1_regb_load, control_unit_1_vram_we, control_unit_1_vram_we_b, not_1_out, or_1_out,
       rgb_video_1_p1, rgb_video_1_p4;
  wire [2:0] control_unit_1_alu_op;
  wire [3:0] ram8_1_out_5, ram8_1_out_5_2, Reg_A_q, Reg_A_q_2, RegB_q, RegB_q_2;
  wire [7:0] adder_1_out, adder_2_out, alu_1_result, counter_1_q, instructionregister_1_opcode,
       instructionregister_1_operand, multiplexer_1_out, multiplexer_2_out, multiplexer_3_out,
       multiplexer_4_out, multiplexer_5_out, multiplexer_6_out, programcounter_1_pc;
  wire [15:0] rom8_1_instruction;

  // Probe on {Reg_A_q_2, Reg_A_q}
  ProgramCounter programcounter_1 (
    .CLK(and_1_out), .Reset(Reset), .Inc(control_unit_1_pc_inc), .D(instructionregister_1_operand),
    .Load(or_1_out), .PC(programcounter_1_pc));
  // Probe on adder_1_out
  Adder adder_1 (.a({Reg_A_q_2, Reg_A_q}), .b(8'h1), .out(adder_1_out));  // open: cin, cout
  Hex_Digit_Display hex_digit_display_1 (.value(RegB_q_2));  // open: dp
  Hex_Digit_Display hex_digit_display_2 (.value(RegB_q));  // open: dp
  Rigester8 RegB (
    .D(multiplexer_4_out), .CLK(and_1_out), .Reset(Reset), .Load(control_unit_1_regb_load),
    .Q({RegB_q_2, RegB_q}));
  // Probe on nothing
  Hex_Digit_Display hex_digit_display_3 (.value(Reg_A_q_2));  // open: dp
  ALU alu_1 (
    .A({Reg_A_q_2, Reg_A_q}), .B({RegB_q_2, RegB_q}), .Op(control_unit_1_alu_op), .Result(alu_1_result));  // open: out_4
  Hex_Digit_Display hex_digit_display_4 (.value(Reg_A_q));  // open: dp
  ROM8 rom8_1 (.Address(programcounter_1_pc), .Instruction(rom8_1_instruction));
  Multiplexer #(.width(8)) multiplexer_1 (
    .in0(instructionregister_1_operand), .in1(alu_1_result), .out(multiplexer_1_out),
    .sel(control_unit_1_alu_store));
  Counter counter_1 (.clr(Reset), .up(1'b1), .clk(and_1_out), .Q(counter_1_q));  // open: load, count, D, carry
  Rigester8 Reg_A (
    .D(multiplexer_3_out), .CLK(and_1_out), .Reset(Reset), .Load(control_unit_1_rega_load),
    .Q({Reg_A_q_2, Reg_A_q}));
  // Probe on instructionregister_1_operand
  InstructionRegister instructionregister_1 (
    .Instruction(rom8_1_instruction), .Load(control_unit_1_ir_load), .CLK(and_1_out), .Reset(Reset),
    .Operand(instructionregister_1_operand), .Opcode(instructionregister_1_opcode));
  // Probe on {RegB_q_2, RegB_q}
  Multiplexer #(.width(8)) multiplexer_2 (
    .in0(adder_1_out), .in1(multiplexer_1_out), .out(multiplexer_2_out), .sel(control_unit_1_inc));
  // Probe on multiplexer_3_out
  and and_1 (and_1_out, not_1_out, clock_1_out);
  Adder adder_2 (.a({RegB_q_2, RegB_q}), .b(8'h1), .out(adder_2_out));  // open: cin, cout
  Hex_Digit_Display hex_digit_display_5 (.value(counter_1_q[7:4]));  // open: dp
  Multiplexer #(.width(8)) multiplexer_3 (
    .in0(multiplexer_2_out), .in1(instructionregister_1_operand), .out(multiplexer_3_out),
    .sel(control_unit_1_rega_load));
  Clock clock_1 (.out(clock_1_out));
  // Probe on adder_2_out
  Hex_Digit_Display hex_digit_display_6 (.value(counter_1_q[3:0]));  // open: dp
  // Probe on control_unit_1_rega_load
  not not_1 (not_1_out, control_unit_1_hlt);
  Multiplexer #(.width(8)) multiplexer_4 (
    .in0(instructionregister_1_operand), .in1(adder_2_out), .out(multiplexer_4_out),
    .sel(control_unit_1_inc_b));
  // Probe on multiplexer_4_out
  // Probe on instructionregister_1_operand
  Comparator #(.mode("unsigned")) comparator_1 (
    .a({Reg_A_q_2, Reg_A_q}), .b({8{1'b0}}), .eq(comparator_1_eq));  // open: gt, lt
  Multiplexer #(.width(8)) multiplexer_5 (
    .in0(instructionregister_1_operand), .in1(RAM_Addr_Monitor), .out(multiplexer_5_out), .sel(Monitor_Mode));
  Hex_Digit_Display hex_digit_display_7 (.value(ram8_1_out_5_2));  // open: dp
  Hex_Digit_Display hex_digit_display_8 (.value(ram8_1_out_5));  // open: dp
  RAM8 ram8_1 (
    .Address(multiplexer_5_out), .WE(control_unit_1_ram_we), .CLK(and_1_out), .DataIn({Reg_A_q_2, Reg_A_q}),
    .out_5({ram8_1_out_5_2, ram8_1_out_5}));
  or or_1 (or_1_out, control_unit_1_pc_load, control_unit_1_jz_out);
  Multiplexer #(.width(8)) multiplexer_6 (
    .in0(instructionregister_1_operand), .in1({RegB_q_2, RegB_q}), .out(multiplexer_6_out),
    .sel(control_unit_1_vram_we_b));
  // RGB_Video #(.height(16), .scale(8), .width(16)) rgb_video_1: pin names not known; wires that end beside it: rgb_video_1_p1, Reset, and_1_out, rgb_video_1_p4, multiplexer_6_out[3:0], rgb_video_1_p1, multiplexer_6_out[7:4], {Reg_A_q_2, Reg_A_q}
  // Probe on multiplexer_6_out
  // Probe on {Reg_A_q_2, Reg_A_q}
  Control_Unit control_unit_1 (
    .Opcode(instructionregister_1_opcode), .ZeroFlag(comparator_1_eq), .IR_Load(control_unit_1_ir_load),
    .RegB_Load(control_unit_1_regb_load), .ALU_Store(control_unit_1_alu_store),
    .ALU_Op(control_unit_1_alu_op), .HLT(control_unit_1_hlt), .PC_Inc(control_unit_1_pc_inc),
    .RAM_WE(control_unit_1_ram_we), .RegA_Load(control_unit_1_rega_load), .PC_Load(control_unit_1_pc_load),
    .JZ_OUT(control_unit_1_jz_out), .VRAM_WE(control_unit_1_vram_we), .Inc(control_unit_1_inc),
    .VRAM_WE_B(control_unit_1_vram_we_b), .INC_B(control_unit_1_inc_b));  // open: RAM_RE
  or or_2 (rgb_video_1_p4, control_unit_1_vram_we, control_unit_1_vram_we_b);
endmodule
